# Fritzing sketch AddressibleLED-Controller (saved by Fritzing 1.0.0rc)
breadboards: 3

parts:
  IC3 = Buck Converter 12v->5v (Inline) [chip_label="Buck Cnv" package="DIP (Dual Inline) [THT]"]
  J5 = Camdenboss CTB0158-3 [part_number=CTB0158-3 package=THT]
  J6 = Camdenboss CTB0158-3 [part_number=CTB0158-3 package=THT]
  M3 = ESP32-S3-DevKitC-1-N8R8-v1 [part_number=ESP32-S3-DevKitC-1-N8R8-v1]
  U3 = 74AHCT125 [part_number=SN74AHCT125 package=dil14]
  R5 = Resistor [tolerance=±5% power=0.25W resistance=330 package=THT]
  R6 = Resistor [tolerance=±5% power=0.25W resistance=330 package=THT]
  C2 = Ceramic Capacitor [capacitance=100nF voltage=25V package="200 mil [THT, multilayer]"]
  J7 = Screw terminal - 2 pins [package=THT]
  WS1 = WS2811 RGB LED strip (12V)
  WS2 = WS2811 RGB LED strip (12V)
  C5 = Electrolytic Capacitor [capacitance=1mF voltage=16V package="200 mil [THT, electrolytic]"]
  C6 = Electrolytic Capacitor [capacitance=1mF voltage=16V package="200 mil [THT, electrolytic]"]

nets (from the schematic view):
  N1: IC3.VIN+, J5.pin3, J6.pin3, J7.pin2
  N2: IC3.VIN-, J5.pin1, J6.pin1, J7.pin1
  N3: IC3.VOUT-, M3.pin_22, M3.pin_23, M3.pin_24, M3.pin_44, U3.1OE, U3.2OE, U3.GND, C2.1
  N4: IC3.VOUT+, M3.pin_21, U3.4OE
  N5: J5.pin2, R6.Pin_0
  N6: J5.terminal_1, WS1.GND, C5.+
  N7: J5.terminal_2, WS1.DIN
  N8: J5.terminal_3, WS1.12V, C5.-
  N9: J6.pin2, R5.Pin_0
  N10: J6.terminal_1, WS2.GND, C6.+
  N11: J6.terminal_2, WS2.DIN
  N12: J6.terminal_3, WS2.12V, C6.-
  N13: M3.pin_1, M3.pin_2
  N14: M3.pin_5, U3.2A
  N15: M3.pin_6, U3.1A
  N16: U3.1Y, R6.Pin_1
  N17: U3.2Y, R5.Pin_1
  N18: U3.3OE, U3.VCC, C2.0

notes:
  12v DC Power Source
  (5A for 2 LED strings)
  18Gauge 3-wire cables from
  controller terminals to LED strip (Cap at LED end)

custom parts:
  Buck Converter 12v->5v (Inline): In-line waterproof DC-DC buck converter, 12V in, 5V out, 3A
  ESP32-S3-DevKitC-1-N8R8-v1: ESP32-S3-DevKitC-1-N8R8-v1 This module is 44pins long (2x22) and 11 pins width.
  74AHCT125: Quad Level-Shifter (3V to 5V) Quadruple Bus Buffer Gates With 3-State Outputs
  WS2811 RGB LED strip (12V): WS2811 strip
