# Fritzing sketch ESP-to-LED-Strip (saved by Fritzing 1.0.0rc)
circuit board: 5.42348cm x 5.17881cm
breadboards: 1

parts:
  WeMos_D1_Mini1 = WeMos D1 Mini
  U1 = WS2812 RGB LED strip
  R1 = Resistor [tolerance=±5% power=0.25W resistance=330 package=THT]
  J1 = Power Jack [package=power_jack_combo]

nets:
  5V: WeMos_D1_Mini1.5V, U1.VCC, J1.PWR
  N1: WeMos_D1_Mini1.D4, R1.Pin_0
  GND: WeMos_D1_Mini1.G, U1.GND, J1.GND
  N2: U1.DIN, R1.Pin_1

custom parts:
  WS2812 RGB LED strip: WS2812 strip
