# Fritzing sketch ESP-to-mini-LED-Strip (saved by Fritzing 1.0.0rc)
breadboards: 1

parts:
  WeMos_D1_Mini2 = WeMos D1 Mini
  Mini-LED_Strip1 = Header 2 [package=screwterminal-3.5mm-2_lock]
  R1 = Resistor [tolerance=±5% power=0.25W resistance=100k package=THT]
  R2 = Resistor [tolerance=±5% power=0.25W resistance=1k package=THT]
  NPN = NPN-Transistor [package="TO92 [THT]"]
  S1 = SWITCH-MOMENTARY-2 [package=tactile-switch-1101ne]

nets:
  N1: WeMos_D1_Mini2.3V3, Mini-LED_Strip1.1
  N2: WeMos_D1_Mini2.D1, S1.1
  N3: WeMos_D1_Mini2.D5, R1.Pin_0, R2.Pin_0, R2.Pin_1, NPN.B
  N4: WeMos_D1_Mini2.G, R1.Pin_1, NPN.E, S1.2
  N5: Mini-LED_Strip1.2, NPN.C
