# Fritzing sketch Outdoor-LED-Controller (saved by Fritzing 1.0.0rc)
circuit board: 5.42348cm x 5.17881cm
breadboards: 3

parts:
  Buck_Converter_(12v_to_5v) = Buck Converter 12v->5v (Inline) [chip_label="Buck Cnv" package="DIP (Dual Inline) [THT]"]
  Screw_Terminal = Camdenboss CTB0158-3 [part_number=CTB0158-3 package=THT]
  Screw_Terminal_2 = Camdenboss CTB0158-3 [part_number=CTB0158-3 package=THT]
  WLED_Controller = ESP32-S3-DevKitC-1-N8R8-v1 [part_number=ESP32-S3-DevKitC-1-N8R8-v1]
  Level_Converter_(3_3v_to_5v) = 74AHCT125 [part_number=SN74AHCT125 package=dil14]
  R5 = Resistor [tolerance=±5% power=0.25W resistance=330 package=THT]
  R6 = Resistor [tolerance=±5% power=0.25W resistance=330 package=THT]
  C2 = Ceramic Capacitor [capacitance=100nF voltage=25V package="200 mil [THT, multilayer]"]
  12v_DC_Power_Supply = Screw terminal - 2 pins [package=THT]
  LED_String = WS2811 RGB LED strip (12V)
  LED_String_2 = WS2811 RGB LED strip (12V)
  C5 = Electrolytic Capacitor [capacitance=1mF voltage=16V package="200 mil [THT, electrolytic]"]
  C6 = Electrolytic Capacitor [capacitance=1mF voltage=16V package="200 mil [THT, electrolytic]"]
  Fuse_Holder2 = Fuse Holder - Mini Blade (SL-506P / SL-506P-B) PCB 4-pin [part_number=SL-506P package=THT]
  Fuse_Holder1 = Fuse Holder - Mini Blade (SL-506P / SL-506P-B) PCB 4-pin [part_number=SL-506P package=THT]

nets (from the schematic view):
  N1: Buck_Converter_(12v_to_5v).VIN+, 12v_DC_Power_Supply.pin2, Fuse_Holder2.B_(pin_1), Fuse_Holder2.B_(pin_2), Fuse_Holder1.B_(pin_1), Fuse_Holder1.B_(pin_2)
  N2: Buck_Converter_(12v_to_5v).VIN-, Screw_Terminal.pin1, Screw_Terminal_2.pin1, 12v_DC_Power_Supply.pin1
  N3: Buck_Converter_(12v_to_5v).VOUT-, WLED_Controller.pin_22, WLED_Controller.pin_23, WLED_Controller.pin_24, WLED_Controller.pin_44, Level_Converter_(3_3v_to_5v).1OE, Level_Converter_(3_3v_to_5v).2OE, Level_Converter_(3_3v_to_5v).GND, C2.1
  N4: Buck_Converter_(12v_to_5v).VOUT+, WLED_Controller.pin_21, Level_Converter_(3_3v_to_5v).4OE
  N5: Screw_Terminal.pin2, R6.Pin_0
  N6: Screw_Terminal.pin3, Fuse_Holder2.A_(pin_1), Fuse_Holder2.A_(pin_2)
  N7: Screw_Terminal.terminal_1, LED_String.GND, C5.+
  N8: Screw_Terminal.terminal_2, LED_String.DIN
  N9: Screw_Terminal.terminal_3, LED_String.12V, C5.-
  N10: Screw_Terminal_2.pin2, R5.Pin_0
  N11: Screw_Terminal_2.pin3, Fuse_Holder1.A_(pin_1), Fuse_Holder1.A_(pin_2)
  N12: Screw_Terminal_2.terminal_1, LED_String_2.GND, C6.+
  N13: Screw_Terminal_2.terminal_2, LED_String_2.DIN
  N14: Screw_Terminal_2.terminal_3, LED_String_2.12V, C6.-
  N15: WLED_Controller.pin_1, WLED_Controller.pin_2
  N16: WLED_Controller.pin_5, Level_Converter_(3_3v_to_5v).2A
  N17: WLED_Controller.pin_6, Level_Converter_(3_3v_to_5v).1A
  N18: Level_Converter_(3_3v_to_5v).1Y, R6.Pin_1
  N19: Level_Converter_(3_3v_to_5v).2Y, R5.Pin_1
  N20: Level_Converter_(3_3v_to_5v).3OE, Level_Converter_(3_3v_to_5v).VCC, C2.0

notes:
  12v DC Power Source
  (5A for 2 LED strings)
  18Gauge 3-wire cables from
  controller terminals to LED strip (Cap at LED end)

custom parts:
  Buck Converter 12v->5v (Inline): In-line waterproof DC-DC buck converter, 12V in, 5V out, 3A
  ESP32-S3-DevKitC-1-N8R8-v1: ESP32-S3-DevKitC-1-N8R8-v1 This module is 44pins long (2x22) and 11 pins width.
  74AHCT125: Quad Level-Shifter (3V to 5V) Quadruple Bus Buffer Gates With 3-State Outputs
  WS2811 RGB LED strip (12V): WS2811 strip
